# Fritzing sketch knockknock (saved by Fritzing 0.9.3b)
breadboards: 1

parts:
  Arduino1 = Arduino Uno (Rev3)
  J1 = Piezo Speaker
  R1 = Textile Analog Pressure Sensor [part_number=PW073]

nets:
  N1: Arduino1.A0, Arduino1.GND, J1.pin1, R1.pin_1
  N2: Arduino1.D9_PWM, J1.pin2

notes:
  KnockKnock with sequence memory
  This experiment uses a piezo buzzer as a vibration sensor wired to an analog input.
  Don't get confused with the piezo sensor as input and piezo buzzer as output!
  Code must be changed if you use a standard button on a regular digital pin.
  Also, be sure what kind of sound buzzer you have, is it an active or passive sound buzzer?
  This experiment uses a passive sound buzzer.
  The knock sensor is a piezo buzzer coupled with a resistor and diodes to protect the arduino pins.
  http://electronics.stackexchange.com/questions/216274/arduino-piezo-vibration-measurement-circuit
  Zafar Iqbal, Vagelis Chantzis
  Arduino Day 2017
  Athens, Greece

// code stored in the sketch: Button.ino
/*
  Button
 
 Turns on and off a light emitting diode(LED) connected to digital  
 pin 13, when pressing a pushbutton attached to pin 2. 
 
 
 The circuit:
 * LED attached from pin 13 to ground 
 * pushbutton attached to pin 2 from +5V
 * 10K resistor attached to pin 2 from ground
 
 * Note: on most Arduinos there is already an LED on the board
 attached to pin 13.
 
 
 created 2005
 by DojoDave <http://www.0j0.org>
 modified 30 Aug 2011
 by Tom Igoe
 
 This example code is in the public domain.
 
 http://www.arduino.cc/en/Tutorial/Button
 */

// constants won't change. They're used here to 
// set pin numbers:
const int buttonPin = 2;     // the number of the pushbutton pin
const int ledPin =  13;      // the number of the LED pin

// variables will change:
int buttonState = 0;         // variable for reading the pushbutton status

void setup() {
  // initialize the LED pin as an output:
  pinMode(ledPin, OUTPUT);      
  // initialize the pushbutton pin as an input:
  pinMode(buttonPin, INPUT);     
}

void loop(){
  // read the state of the pushbutton value:
  buttonState = digitalRead(buttonPin);

  // check if the pushbutton is pressed.
  // if it is, the buttonState is HIGH:
  if (buttonState == HIGH) {     
    // turn LED on:    
    digitalWrite(ledPin, HIGH);  
  } 
  else {
    // turn LED off:
    digitalWrite(ledPin, LOW); 
  }
}
